# Fritzing sketch app_circuit (saved by Fritzing 0.9.3b)
stripboards: 1

parts:
  Part1 = Arduino Mega 2560 (Rev3)
  hc-sr1 = hc-sr04
  hc-sr2 = hc-sr04
  hc-sr4 = hc-sr04
  M1 = fc-51 [package=THT]
  M2 = fc-51 [package=THT]
  S1 = H-Bridge with L298N
  U1 = SWITCH-SPST-2 [package=switch-spst-vertical]
  A1 = WMYCONGCONG buck converter
  M3 = DC Motor
  J1 = Basic Servo
  JACK1 = 2.1mm Barrel Jack with Terminal Block

nets:
  N1: Part1.D18/TX1, U1.O
  N2: Part1.D11_PWM, S1.ENA
  N3: Part1.D10_PWM, J1.pulse
  GND: Part1.GND, hc-sr1.GND, hc-sr2.GND, hc-sr4.GND, M1.pin2, M2.pin2, U1.P, A1.Pin_3
  VCC: Part1.VIN, hc-sr1.VCC, hc-sr2.VCC, hc-sr4.VCC, M1.pin3, M2.pin3, A1.Pin_4
  N4: Part1.D2_PWM, hc-sr2.Echo
  N5: Part1.D3_PWM, hc-sr2.Trig
  N6: Part1.D4_PWM, hc-sr4.Trig
  N7: Part1.D5_PWM, hc-sr4.Echo
  N8: Part1.D6_PWM, hc-sr1.Echo
  N9: Part1.D7_PWM, hc-sr1.Trig
  N10: Part1.D22, M1.pin1
  N11: Part1.D23, M2.pin1
  N12: Part1.D52, S1.IN2
  N13: Part1.D53, S1.IN1
  N14: S1.12V, A1.Pin_2, JACK1.POS
  GND_2: S1.GND, A1.Pin_1, J1.gnd, JACK1.NEG
  5V: S1.5V, J1.vcc
  N15: S1.M1-01, M3.pin_1
  N16: S1.M1-02, M3.pin_2

custom parts:
  H-Bridge with L298N: h-bridge
  WMYCONGCONG buck converter: These amazing little DC-DC converters feature a wide input voltage of 4.5-24V and the output voltage can be set to one of six fixed voltages, or fully variable, just by bridging the relevant solder pads on the back of the PCB..
